// Logisim project HA_FA.circ as structural Verilog: 2 circuits, main circuit main
module main (
  input  Cin,
  input  A,
  input  B,
  output Q,
  output Cout
);

  wire AND_1_out, AND_2_out, XOR1_out;

  xor XOR1 (XOR1_out, A, B);
  and AND_1 (AND_1_out, B, A);
  and AND_2 (AND_2_out, Cin, XOR1_out);
  xor XOR2 (Q, XOR1_out, Cin);
  or OR_1 (Cout, AND_2_out, AND_1_out);

  // Notes on the sheet:
  //   1
  //   Meio Somador (HA)
  //   S o m  a d o r  T o t a l  ( F A )
endmodule

module Somador_1_bit (
  input  A,
  input  Cin,
  input  B,
  output S,
  output Cout
);

  wire AND1_out, AND2_out, multiplexer_1_out, not_1_out, XOR1_out;

  not not_1 (not_1_out, B);
  Multiplexer #(.enable("false")) multiplexer_1 (.in0(B), .in1(not_1_out), .out(multiplexer_1_out), .sel(Cin));
  xor XOR1 (XOR1_out, A, multiplexer_1_out);
  and AND1 (AND1_out, multiplexer_1_out, A);
  main main_1 ();  // open: A, B, Cin, Q, Cout
  and AND2 (AND2_out, Cin, XOR1_out);
  xor XOR2 (S, XOR1_out, Cin);
  or OR1 (Cout, AND2_out, AND1_out);

  // Notes on the sheet:
  //   COMPLEMENTO DE 2
  //   COMPLEMENTO DE 1
endmodule
