// Logisim project MUX 2 X 1 5 BITS.circ as structural Verilog: 1 circuit, main circuit main
// M 2 X 1
module main (
  input  B_4,
  input  B_3,
  input  B_2,
  input  B_1,
  input  B_0,
  input  A_4,
  input  A_3,
  input  A_2,
  input  A_1,
  input  A_0,
  input  S,
  output Y_3,
  output Y_3_2,
  output Y_2,
  output Y_1,
  output Y_0
);

  // MUX_2_X_1_main main_1: pin names not known; wires that end beside it: B_4, A_4, Y_3, S
  // MUX_2_X_1_main main_2: pin names not known; wires that end beside it: B_3, A_3, Y_3_2, S
  // MUX_2_X_1_main main_3: pin names not known; wires that end beside it: B_2, A_2, Y_2, S
  // MUX_2_X_1_main main_4: pin names not known; wires that end beside it: B_1, A_1, Y_1, S
  // MUX_2_X_1_main main_5: pin names not known; wires that end beside it: B_0, A_0, Y_0, S
endmodule
