// Logisim project SOMADOR CSA 8 BITS_CLA.circ as structural Verilog: 1 circuit, main circuit main
module main (
  input  Cin,
  input  A_0,
  input  B_0,
  input  A_1,
  input  B_1,
  input  A_2,
  input  B_2,
  input  A_3,
  input  B_3,
  input  A_4,
  input  B_4,
  input  A_5,
  input  B_5,
  input  A_6,
  input  B_6,
  input  A_7,
  input  B_7,
  output Q_0,
  output Q_1,
  output Q_2,
  output Q_3,
  output Q_4,
  output Q_5,
  output Q_6,
  output Q_7,
  output Cout
);

  wire main_1_cout, main_2_cout, main_2_q0, main_2_q1, main_2_q2, main_2_q3, main_3_cout, main_3_q0,
       main_3_q1, main_3_q2, main_3_q3;

  SOMADOR_CLA_4_Bits_main main_1 (
    .Cin(Cin), .A0(A_0), .B0(B_0), .A1(A_1), .B1(B_1), .A2(A_2), .B2(B_2), .A3(A_3), .B3(B_3), .Q0(Q_0),
    .Q1(Q_1), .Q2(Q_2), .Q3(Q_3), .Cout(main_1_cout));  // open: in_10
  SOMADOR_CLA_4_Bits_main main_2 (
    .Cin(1'b0), .A0(A_4), .B0(B_4), .A1(A_5), .B1(B_5), .A2(A_6), .B2(B_6), .A3(A_7), .B3(B_7),
    .Q0(main_2_q0), .Q1(main_2_q1), .Q2(main_2_q2), .Q3(main_2_q3), .Cout(main_2_cout));  // open: in_10
  SOMADOR_CLA_4_Bits_main main_3 (
    .Cin(1'b1), .A0(A_4), .B0(B_4), .A1(A_5), .B1(B_5), .A2(A_6), .B2(B_6), .A3(A_7), .B3(B_7),
    .Q0(main_3_q0), .Q1(main_3_q1), .Q2(main_3_q2), .Q3(main_3_q3), .Cout(main_3_cout));  // open: in_10
  // MUX_2_X_1_5_BITS_main main_4: pin names not known; wires that end beside it: main_2_q0, main_2_q1, main_2_q2, main_2_q3, main_2_cout, main_3_q0, main_3_q1, main_3_q2, main_3_q3, main_3_cout, main_1_cout, Q_4, Q_5, Q_6, Q_7, Cout
endmodule
