// Logisim project SS_XOR_MUX.circ as structural Verilog: 2 circuits, main circuit main
module main (
  input  A,
  input  Cin,
  input  B,
  input  A_2,
  input  Cin_2,
  input  B_2,
  input  in_7,
  output Q,
  output Cout,
  output Q_2,
  output Cout_2
);

  wire AND_1_2_out, AND_1_out, AND_2_2_out, AND_2_out, multiplexer_1_out, not_1_out, XOR1_2_out, XOR1_out,
       XOR3_out;

  xor XOR3 (XOR3_out, Cin, B);
  not not_1 (not_1_out, B_2);
  Multiplexer #(.enable("false")) multiplexer_1 (.in0(B_2), .in1(not_1_out), .out(multiplexer_1_out), .sel(Cin_2));
  xor XOR1 (XOR1_out, A, XOR3_out);
  and AND_1 (AND_1_out, XOR3_out, A);
  xor XOR1_2 (XOR1_2_out, A_2, multiplexer_1_out);
  and AND_1_2 (AND_1_2_out, multiplexer_1_out, A_2);
  and AND_2 (AND_2_out, Cin, XOR1_out);
  and AND_2_2 (AND_2_2_out, Cin_2, XOR1_2_out);
  xor XOR2 (Q, XOR1_out, Cin);
  or OR_1 (Cout, AND_2_out, AND_1_out);
  xor XOR2_2 (Q_2, XOR1_2_out, Cin_2);
  or OR_1_2 (Cout_2, AND_2_2_out, AND_1_2_out);

  // Notes on the sheet:
  //   2
  //   Somador Subtrator XOR
  //   Somador Subtrator Multipexador
endmodule

module Somador_1_bit (
  input  A,
  input  Cin,
  input  B,
  output S,
  output Cout
);

  wire AND1_out, AND2_out, multiplexer_1_out, not_1_out, XOR1_out;

  not not_1 (not_1_out, B);
  Multiplexer #(.enable("false")) multiplexer_1 (.in0(B), .in1(not_1_out), .out(multiplexer_1_out), .sel(Cin));
  xor XOR1 (XOR1_out, A, multiplexer_1_out);
  and AND1 (AND1_out, multiplexer_1_out, A);
  main main_1 ();  // open: A, Cin, B, A_2, Cin_2, B_2, in_7, Q, Cout, Q_2, Cout_2
  and AND2 (AND2_out, Cin, XOR1_out);
  xor XOR2 (S, XOR1_out, Cin);
  or OR1 (Cout, AND2_out, AND1_out);

  // Notes on the sheet:
  //   COMPLEMENTO DE 2
  //   COMPLEMENTO DE 1
endmodule
