// Logisim project RCA 2 BITS.circ as structural Verilog: 2 circuits, main circuit main
module main (
  input  A_0,
  input  Cin,
  input  B_0,
  input  A_1,
  input  B_1,
  input  in_6,
  output Q_0,
  output Q_1,
  output Cout
);

  wire AND_1_2_out, AND_1_out, AND_2_2_out, AND_2_out, OR_1_out, XOR1_2_out, XOR1_out;

  xor XOR1 (XOR1_out, A_0, B_0);
  and AND_1 (AND_1_out, B_0, A_0);
  xor XOR1_2 (XOR1_2_out, A_1, B_1);
  and AND_1_2 (AND_1_2_out, B_1, A_1);
  and AND_2 (AND_2_out, Cin, XOR1_out);
  and AND_2_2 (AND_2_2_out, OR_1_out, XOR1_2_out);
  xor XOR2 (Q_0, XOR1_out, Cin);
  or OR_1 (OR_1_out, AND_2_out, AND_1_out);
  xor XOR2_2 (Q_1, XOR1_2_out, OR_1_out);
  or OR_1_2 (Cout, AND_2_2_out, AND_1_2_out);

  // Notes on the sheet:
  //   3
  //   Somador RCA 2 Bits
endmodule

module Somador_1_bit (
  input  A,
  input  Cin,
  input  B,
  output S,
  output Cout
);

  wire AND1_out, AND2_out, multiplexer_1_out, not_1_out, XOR1_out;

  not not_1 (not_1_out, B);
  Multiplexer #(.enable("false")) multiplexer_1 (.in0(B), .in1(not_1_out), .out(multiplexer_1_out), .sel(Cin));
  xor XOR1 (XOR1_out, A, multiplexer_1_out);
  and AND1 (AND1_out, multiplexer_1_out, A);
  main main_1 ();  // open: A_0, Cin, B_0, A_1, B_1, in_6, Q_0, Q_1, Cout
  and AND2 (AND2_out, Cin, XOR1_out);
  xor XOR2 (S, XOR1_out, Cin);
  or OR1 (Cout, AND2_out, AND1_out);

  // Notes on the sheet:
  //   COMPLEMENTO DE 2
  //   COMPLEMENTO DE 1
endmodule
