// Logisim project SS RCA_MUX.circ as structural Verilog: 2 circuits, main circuit main
module main (
  input  A,
  input  Cin,
  input  B,
  input  A_2,
  input  B_2,
  input  A_3,
  input  Cin_2,
  input  B_3,
  input  A_4,
  input  B_4,
  input  in_11,
  output Q,
  output Q_2,
  output Cout,
  output Q_3,
  output Q_4,
  output Cout_2
);

  wire AND_1_2_out, AND_1_3_out, AND_1_4_out, AND_1_out, AND_2_2_out, AND_2_3_out, AND_2_4_out, AND_2_out,
       multiplexer_1_out, multiplexer_2_out, not_1_out, not_2_out, OR_1_3_out, OR_1_out, XOR1_2_out,
       XOR1_3_out, XOR1_4_out, XOR1_out, XOR3_2_out, XOR3_out;

  not not_1 (not_1_out, B);
  not not_2 (not_2_out, B_2);
  Multiplexer #(.enable("false")) multiplexer_1 (.in0(B), .in1(not_1_out), .out(multiplexer_1_out), .sel(Cin));
  Multiplexer #(.enable("false")) multiplexer_2 (.in0(B_2), .in1(not_2_out), .out(multiplexer_2_out), .sel(Cin));
  xor XOR3 (XOR3_out, B_3, Cin_2);
  xor XOR3_2 (XOR3_2_out, B_4, Cin_2);
  xor XOR1 (XOR1_out, A, multiplexer_1_out);
  xor XOR1_2 (XOR1_2_out, A_2, multiplexer_2_out);
  xor XOR1_3 (XOR1_3_out, A_3, XOR3_out);
  xor XOR1_4 (XOR1_4_out, A_4, XOR3_2_out);
  and AND_1 (AND_1_out, multiplexer_1_out, A);
  and AND_1_2 (AND_1_2_out, multiplexer_2_out, A_2);
  and AND_1_3 (AND_1_3_out, XOR3_out, A_3);
  and AND_1_4 (AND_1_4_out, XOR3_2_out, A_4);
  and AND_2 (AND_2_out, Cin, XOR1_out);
  and AND_2_2 (AND_2_2_out, OR_1_out, XOR1_2_out);
  and AND_2_3 (AND_2_3_out, Cin_2, XOR1_3_out);
  and AND_2_4 (AND_2_4_out, OR_1_3_out, XOR1_4_out);
  xor XOR2 (Q, XOR1_out, Cin);
  or OR_1 (OR_1_out, AND_2_out, AND_1_out);
  xor XOR2_2 (Q_2, XOR1_2_out, OR_1_out);
  or OR_1_2 (Cout, AND_2_2_out, AND_1_2_out);
  xor XOR2_3 (Q_3, XOR1_3_out, Cin_2);
  or OR_1_3 (OR_1_3_out, AND_2_3_out, AND_1_3_out);
  xor XOR2_4 (Q_4, XOR1_4_out, OR_1_3_out);
  or OR_1_4 (Cout_2, AND_2_4_out, AND_1_4_out);

  // Notes on the sheet:
  //   4
  //   Somador Subtrator RCA Multiplexador
  //   Somador Subtrator RCA Xor
endmodule

module Somador_1_bit (
  input  A,
  input  Cin,
  input  B,
  output S,
  output Cout
);

  wire AND1_out, AND2_out, multiplexer_1_out, not_1_out, XOR1_out;

  not not_1 (not_1_out, B);
  Multiplexer #(.enable("false")) multiplexer_1 (.in0(B), .in1(not_1_out), .out(multiplexer_1_out), .sel(Cin));
  xor XOR1 (XOR1_out, A, multiplexer_1_out);
  and AND1 (AND1_out, multiplexer_1_out, A);
  main main_1 ();  // open: A, Cin, B, A_2, B_2, A_3, Cin_2, B_3, A_4, B_4, in_11, Q, Q_2, Cout, Q_3, Q_4, Cout_2
  and AND2 (AND2_out, Cin, XOR1_out);
  xor XOR2 (S, XOR1_out, Cin);
  or OR1 (Cout, AND2_out, AND1_out);

  // Notes on the sheet:
  //   COMPLEMENTO DE 2
  //   COMPLEMENTO DE 1
endmodule
