// Logisim project BIT A BIT 5 BITS.circ as structural Verilog: 1 circuit, main circuit main
// BIT A BIT
module main (
  input  A_0,
  input  A_1,
  input  A_2,
  input  A_3,
  input  A_4,
  input  B_0,
  input  B_1,
  input  B_2,
  input  B_3,
  input  B_4,
  output NAND_0,
  output NAND_1,
  output NAND_2,
  output NAND_3,
  output NAND_4,
  output NOR_0,
  output NOR_1,
  output NOR_2,
  output NOR_3,
  output NOR_4,
  output XOR_0,
  output XOR_1,
  output XOR_2,
  output XOR_3,
  output XOR_4
);

  // BIT_A_BIT_main main_1: pin names not known; wires that end beside it: A_0, B_0, NAND_0, NOR_0, XOR_0
  // BIT_A_BIT_main main_2: pin names not known; wires that end beside it: A_1, B_1, NAND_1, NOR_1, XOR_1
  // BIT_A_BIT_main main_3: pin names not known; wires that end beside it: A_2, B_2, NAND_2, NOR_2, XOR_2
  // BIT_A_BIT_main main_4: pin names not known; wires that end beside it: A_3, B_3, NAND_3, NOR_3, XOR_3
  // BIT_A_BIT_main main_5: pin names not known; wires that end beside it: A_4, B_4, NAND_4, NOR_4, XOR_4
endmodule
