// Logisim project COMPARADOR 5 BITS.circ as structural Verilog: 1 circuit, main circuit main
// COMP
module main (
  input  Q_4,
  input  Q_3,
  input  Q_2,
  input  Q_1,
  input  Q_0,
  input  Cout,
  input  C_2,
  input  A_0,
  input  A_1,
  input  A_2,
  input  A_3,
  input  A_4,
  input  B_0,
  input  B_1,
  input  B_2,
  input  B_3,
  input  B_4,
  output OVER_FLOW,
  output Q___0,
  output A___0,
  output A___B,
  output B___0,
  output A___B_2
);

  wire _4_out, _5_out, _6_out, _8_out, _11_out, _12_out, _13_out;

  nor _1 (Q___0, Q_4, Q_3, Q_2, Q_1, Q_0);
  nor _2 (A___0, A_0, A_1, A_2, A_3, A_4);
  nor _3 (B___0, B_0, B_1, B_2, B_3, B_4);
  not _11 (_11_out, Q___0);
  xnor _8 (_8_out, A_4, B_4);
  not _12 (_12_out, A_4);
  not _13 (_13_out, A___B);
  and _4 (_4_out, Cout, _11_out, _8_out);
  and _5 (_5_out, _11_out, _12_out, B_4);
  and _6 (_6_out, _11_out, _12_out, B___0);
  and _7 (A___B_2, _13_out, _11_out);
  xor _9 (OVER_FLOW, C_2, Cout);
  or _10 (A___B, _4_out, _5_out, _6_out);
endmodule
