// Logisim project DESLOCAMENTO 5 BITS.circ as structural Verilog: 1 circuit, main circuit main
// DESL
module main (
  input  D_4,
  input  D_3,
  input  D_2,
  input  D_1,
  input  D_0,
  input  S_0,
  input  S1,
  output Y_4,
  output Y_3,
  output Y_2,
  output Y_1,
  output Y_0
);

  wire main_1_p5, main_1_p6, main_1_p7, main_1_p8, main_2_p7, main_2_p8, main_2_p9, main_2_p10, main_3_p7,
       main_3_p8, main_3_p9, main_3_p10, main_4_p7, main_4_p8, main_4_p9;

  // FIM_main main_1: pin names not known; wires that end beside it: S_0, S1, D_4, Y_4, main_1_p5, main_1_p6, main_1_p7, main_1_p8
  // MEIO_main main_2: pin names not known; wires that end beside it: main_1_p5, main_1_p6, main_1_p7, main_1_p8, D_3, Y_3, main_2_p7, main_2_p8, main_2_p9, main_2_p10
  // MEIO_main main_3: pin names not known; wires that end beside it: main_2_p7, main_2_p8, main_2_p9, main_2_p10, D_2, Y_2, main_3_p7, main_3_p8, main_3_p9, main_3_p10
  // MEIO_main main_4: pin names not known; wires that end beside it: main_3_p7, main_3_p8, main_3_p9, main_3_p10, D_1, Y_1, main_4_p7, main_4_p8, main_4_p9
  // INÍCIO_main main_5: pin names not known; wires that end beside it: main_4_p7, main_4_p8, main_4_p9, D_0, Y_0
endmodule
