// Logisim project ULA 5 BITS.circ as structural Verilog: 1 circuit, main circuit main
module main (
  input  Cin,
  input  S_3,
  input  S_2,
  input  S_1,
  input  S_0,
  input  A_0,
  input  A_1,
  input  A_2,
  input  A_3,
  input  A_4,
  input  B_0,
  input  B_1,
  input  B_2,
  input  B_3,
  input  B_4,
  output Q_0,
  output Q_1,
  output Q_2,
  output Q_3,
  output Q_3_2,
  output Cout,
  output OVER_FLOW,
  output A___B,
  output A___0,
  output B___0,
  output A___B_2,
  output A___B_3
);

  wire main_1_nand_0, main_1_nand_1, main_1_nand_2, main_1_nand_3, main_1_nand_4, main_1_nor_0, main_1_nor_1,
       main_1_nor_2, main_1_nor_3, main_1_nor_4, main_1_xor_0, main_1_xor_1, main_1_xor_2, main_1_xor_3,
       main_1_xor_4, main_2_c_4, main_2_q_0, main_2_q_1, main_2_q_2, main_2_q_3, main_2_q_4, main_3_y_0,
       main_3_y_1, main_3_y_2, main_3_y_2_2, main_3_y_2_3, main_4_y_0, main_4_y_1, main_4_y_2, main_4_y_3,
       main_4_y_4, main_5_p12, main_5_p13, main_5_p14, main_5_p15, main_5_p16, main_7_y_0, main_7_y_1,
       main_7_y_2, main_7_y_3, main_7_y_4;

  BIT_A_BIT_5_BITS_main main_1 (
    .A_0(A_0), .A_1(A_1), .A_2(A_2), .A_3(A_3), .A_4(A_4), .B_0(B_0), .B_1(B_1), .B_2(B_2), .B_3(B_3),
    .B_4(B_4), .NAND_0(main_1_nand_0), .NAND_1(main_1_nand_1), .NAND_2(main_1_nand_2),
    .NAND_3(main_1_nand_3), .NAND_4(main_1_nand_4), .NOR_0(main_1_nor_0), .NOR_1(main_1_nor_1),
    .NOR_2(main_1_nor_2), .NOR_3(main_1_nor_3), .NOR_4(main_1_nor_4), .XOR_0(main_1_xor_0),
    .XOR_1(main_1_xor_1), .XOR_2(main_1_xor_2), .XOR_3(main_1_xor_3), .XOR_4(main_1_xor_4));
  \ARITMÉTICA_5_BITS_main  main_2 (
    .A_0(A_0), .B_0(B_0), .A_1(A_1), .B_1(B_1), .A_2(A_2), .B_2(B_2), .A_3(A_3), .B_3(B_3), .A_4(A_4),
    .B_4(B_4), .Cin(Cin), .S_0(S_1), .S_1(S_0), .Q_0(main_2_q_0), .Q_1(main_2_q_1), .Q_2(main_2_q_2),
    .Q_3(main_2_q_3), .Q_4(main_2_q_4), .C_4(main_2_c_4), .Cout(Cout));
  MUX_4_X_1_5_BITS_main main_3 (
    .E_4(main_1_xor_4), .E_3(main_1_xor_3), .E_2(main_1_xor_2), .E_1(main_1_xor_1), .E_0(main_1_xor_0),
    .C_4(main_1_nor_4), .C_3(main_1_nor_3), .C_2(main_1_nor_2), .C_1(main_1_nor_1), .C_0(main_1_nor_0),
    .B_4(main_1_nand_4), .B_3(main_1_nand_3), .B_2(main_1_nand_2), .B_1(main_1_nand_1), .B_0(main_1_nand_0),
    .A_4(A_4), .A_3(A_3), .A_2(A_2), .A_1(A_1), .A_0(A_0), .Y_2(main_3_y_2), .Y_2_2(main_3_y_2_2),
    .Y_2_3(main_3_y_2_3), .Y_1(main_3_y_1), .Y_0(main_3_y_0), .S_1(S_1), .S_0(S_0));
  DESLOCAMENTO_5_BITS_main main_4 (
    .S_0(S_0), .S1(S_1), .D_4(A_4), .D_3(A_3), .D_2(A_2), .D_1(A_1), .D_0(A_0), .Y_4(main_4_y_4),
    .Y_3(main_4_y_3), .Y_2(main_4_y_2), .Y_1(main_4_y_1), .Y_0(main_4_y_0));
  // MUX_2_X_1_5_BITS_main main_5: pin names not known; wires that end beside it: main_4_y_0, main_4_y_1, main_4_y_2, main_4_y_3, main_4_y_4, main_2_q_0, main_2_q_1, main_2_q_2, main_2_q_3, main_2_q_4, S_2, main_5_p12, main_5_p13, main_5_p14, main_5_p15, main_5_p16
  COMPARADOR_5_BITS_main main_6 (
    .A_0(A_0), .A_1(A_1), .A_2(A_2), .A_3(A_3), .A_4(A_4), .B_0(B_0), .B_1(B_1), .B_2(B_2), .B_3(B_3),
    .B_4(B_4), .Q_4(main_2_q_4), .Q_3(main_2_q_3), .Q_2(main_2_q_2), .Q_1(main_2_q_1), .Q_0(main_2_q_0),
    .Cout(Cout), .C_2(main_2_c_4), .OVER_FLOW(OVER_FLOW), .Q___0(A___B), .A___0(A___0), .A___B(A___B_2),
    .B___0(B___0), .A___B_2(A___B_3));
  XOR_5_BITS_main main_7 (
    .E_0(main_3_y_0), .E_1(main_3_y_1), .E_2(main_3_y_2_3), .E_3(main_3_y_2_2), .E_4(main_3_y_2), .S_2(S_2),
    .Y_0(main_7_y_0), .Y_1(main_7_y_1), .Y_2(main_7_y_2), .Y_3(main_7_y_3), .Y_4(main_7_y_4));
  // MUX_2_X_1_5_BITS_main main_8: pin names not known; wires that end beside it: main_7_y_0, main_7_y_1, main_7_y_2, main_7_y_3, main_7_y_4, main_5_p12, main_5_p13, main_5_p14, main_5_p15, main_5_p16, S_3, Q_0, Q_1, Q_2, Q_3, Q_3_2
endmodule
