// Logisim project XOR 5 BITS.circ as structural Verilog: 1 circuit, main circuit main
// XOR
module main (
  input  S_2,
  input  E_0,
  input  E_1,
  input  E_2,
  input  E_3,
  input  E_4,
  output Y_0,
  output Y_1,
  output Y_2,
  output Y_3,
  output Y_4
);

  xor _1 (Y_0, E_0, S_2);
  xor _2 (Y_1, E_1, S_2);
  xor _3 (Y_2, E_2, S_2);
  xor _4 (Y_3, E_3, S_2);
  xor _5 (Y_4, E_4, S_2);
endmodule
