// Logisim project MUX_INVERSOR 10 BITS.circ as structural Verilog: 1 circuit, main circuit main
// XOR 10 BITS
module main (
  input  S_2,
  input  E_0,
  input  E_1,
  input  E_2,
  input  E_3,
  input  E_4,
  input  E_5,
  input  E_6,
  input  E_7,
  input  E_8,
  input  E_9,
  output Y_0,
  output Y_1,
  output Y_2,
  output Y_3,
  output Y_4,
  output Y_5,
  output Y_6,
  output Y_7,
  output Y_8,
  output Y_9
);

  wire not_1_out, not_2_out, not_3_out, not_4_out, not_5_out, not_6_out, not_7_out, not_8_out, not_9_out,
       not_10_out;

  not not_1 (not_1_out, E_0);
  not not_2 (not_2_out, E_1);
  not not_3 (not_3_out, E_2);
  not not_4 (not_4_out, E_3);
  not not_5 (not_5_out, E_4);
  not not_6 (not_6_out, E_5);
  not not_7 (not_7_out, E_6);
  not not_8 (not_8_out, E_7);
  not not_9 (not_9_out, E_8);
  not not_10 (not_10_out, E_9);
  Multiplexer #(.enable("false")) multiplexer_1 (.in0(E_0), .in1(not_1_out), .out(Y_0), .sel(S_2));
  Multiplexer #(.enable("false")) multiplexer_2 (.in0(E_1), .in1(not_2_out), .out(Y_1), .sel(S_2));
  Multiplexer #(.enable("false")) multiplexer_3 (.in0(E_2), .in1(not_3_out), .out(Y_2), .sel(S_2));
  Multiplexer #(.enable("false")) multiplexer_4 (.in0(E_3), .in1(not_4_out), .out(Y_3), .sel(S_2));
  Multiplexer #(.enable("false")) multiplexer_5 (.in0(E_4), .in1(not_5_out), .out(Y_4), .sel(S_2));
  Multiplexer #(.enable("false")) multiplexer_6 (.in0(E_5), .in1(not_6_out), .out(Y_5), .sel(S_2));
  Multiplexer #(.enable("false")) multiplexer_7 (.in0(E_6), .in1(not_7_out), .out(Y_6), .sel(S_2));
  Multiplexer #(.enable("false")) multiplexer_8 (.in0(E_7), .in1(not_8_out), .out(Y_7), .sel(S_2));
  Multiplexer #(.enable("false")) multiplexer_9 (.in0(E_8), .in1(not_9_out), .out(Y_8), .sel(S_2));
  Multiplexer #(.enable("false")) multiplexer_10 (.in0(E_9), .in1(not_10_out), .out(Y_9), .sel(S_2));
endmodule
