// Logisim project ARITMÉTICA 4 BITS.circ as structural Verilog: 1 circuit, main circuit main
// ARITMÉTICA
module main (
  input  S_0,
  input  A_0,
  input  B_0,
  input  A_1,
  input  B_1,
  input  A_2,
  input  B_2,
  input  A_3,
  input  B_3,
  output Q_0,
  output Q_1,
  output Q_2,
  output Q_3,
  output Cout
);

  wire main_1_p5, main_2_p5, main_3_p5;

  // SST_main main_1: pin names not known; wires that end beside it: A_0, B_0, S_0, S_0, main_1_p5, Q_0
  // SST_main main_2: pin names not known; wires that end beside it: A_1, B_1, S_0, main_1_p5, main_2_p5, Q_1
  // SST_main main_3: pin names not known; wires that end beside it: A_2, B_2, S_0, main_2_p5, main_3_p5, Q_2
  // SST_main main_4: pin names not known; wires that end beside it: A_3, B_3, S_0, main_3_p5, Cout, Q_3
endmodule
