// Logisim project INVERSOR.circ as structural Verilog: 1 circuit, main circuit main
// INVERSOR
module main (
  input  E_0,
  input  E_1,
  input  E_2,
  input  E_3,
  input  E_4,
  input  E_5,
  input  E_6,
  input  E_7,
  input  E_8,
  input  E_9,
  input  E_10,
  input  E_11,
  output Y_0,
  output Y_1,
  output Y_2,
  output Y_3,
  output Y_4,
  output Y_5,
  output Y_6,
  output Y_7,
  output Y_8,
  output Y_9,
  output Y_10,
  output Y_11
);

  not not_1 (Y_0, E_0);
  not not_2 (Y_1, E_1);
  not not_3 (Y_2, E_2);
  not not_4 (Y_3, E_3);
  not not_5 (Y_4, E_4);
  not not_6 (Y_5, E_5);
  not not_7 (Y_6, E_6);
  not not_8 (Y_7, E_7);
  not not_9 (Y_8, E_8);
  not not_10 (Y_9, E_9);
  not not_11 (Y_10, E_10);
  not not_12 (Y_11, E_11);
endmodule
