// Logisim project ULA 4 BITS S3.circ as structural Verilog: 1 circuit, main circuit main
module main (
  input  S_2,
  input  S_1,
  input  S_0,
  input  A_0,
  input  B_0,
  input  A_1,
  input  B_1,
  input  A_2,
  input  B_2,
  input  A_3,
  input  B_3,
  output Q_0,
  output Q_1,
  output Q_2,
  output Q_3,
  output Cout
);

  wire main_1_q_0, main_1_q_1, main_1_q_2, main_1_q_3, main_2_p9, main_2_p10, main_2_p11, main_2_p12,
       main_2_p13, main_2_p14, main_2_p15, main_2_p16, main_2_p17, main_2_p18, main_2_p19, main_2_p20,
       main_3_p14, main_3_p15, main_3_p16, main_4_y_0, main_4_y_1, main_4_y_2, main_4_y_3, main_4_y_4,
       main_4_y_5, main_4_y_6, main_4_y_7, main_4_y_8, main_4_y_9, main_4_y_10, main_4_y_11, main_5_p6,
       main_5_p25, main_5_p26, main_5_p27, main_5_p28;

  \ARITMÉTICA_4_BITS_main  main_1 (
    .A_0(A_0), .B_0(B_0), .A_1(A_1), .B_1(B_1), .A_2(A_2), .B_2(B_2), .A_3(A_3), .B_3(B_3), .S_0(S_0),
    .Q_0(main_1_q_0), .Q_1(main_1_q_1), .Q_2(main_1_q_2), .Q_3(main_1_q_3), .Cout(Cout));
  // BIT_A_BIT_4_BITS_main main_2: pin names not known; wires that end beside it: A_0, A_1, A_2, A_3, B_0, B_1, B_2, B_3, main_2_p9, main_2_p10, main_2_p11, main_2_p12, main_2_p13, main_2_p14, main_2_p15, main_2_p16, main_2_p17, main_2_p18, main_2_p19, main_2_p20
  // MUX_4_X_1_4_BITS_main main_3: pin names not known; wires that end beside it: main_1_q_0, main_1_q_1, main_1_q_2, main_1_q_3, main_2_p9, main_2_p10, main_2_p11, main_2_p12, main_2_p13, main_2_p14, main_2_p15, S_1, S_0, main_3_p14, main_3_p15, main_3_p16
  INVERSOR_main main_4 (
    .E_0(main_2_p9), .E_1(main_2_p10), .E_2(main_2_p11), .E_3(main_2_p12), .E_4(main_2_p13),
    .E_5(main_2_p14), .E_6(main_2_p15), .E_7(main_2_p16), .E_8(main_2_p17), .E_9(main_2_p18),
    .E_10(main_2_p19), .E_11(main_2_p20), .Y_0(main_4_y_0), .Y_1(main_4_y_1), .Y_2(main_4_y_2),
    .Y_3(main_4_y_3), .Y_4(main_4_y_4), .Y_5(main_4_y_5), .Y_6(main_4_y_6), .Y_7(main_4_y_7),
    .Y_8(main_4_y_8), .Y_9(main_4_y_9), .Y_10(main_4_y_10), .Y_11(main_4_y_11));
  // MUX_4_X_1_4_BITS_main main_5: pin names not known; wires that end beside it: main_2_p16, main_2_p17, main_2_p18, main_2_p19, main_2_p20, main_5_p6, main_1_q_0, main_1_q_1, main_1_q_2, main_1_q_3, main_4_y_0, main_4_y_1, main_4_y_2, main_4_y_3, main_4_y_4, main_4_y_5, main_4_y_6, main_4_y_7, main_4_y_8, main_4_y_9, main_4_y_10, main_4_y_11, S_1, S_0, main_5_p25, main_5_p26, main_5_p27, main_5_p28
  // MUX_2_X_1_4_BITS_main main_6: pin names not known; wires that end beside it: main_3_p14, main_3_p15, main_3_p16, main_5_p6, main_5_p25, main_5_p26, main_5_p27, main_5_p28, S_2, Q_0, Q_1, Q_2, Q_3
endmodule
