// Logisim project SOMADOR CSA 8 BITS_RCA.circ as structural Verilog: 1 circuit, main circuit main
module main (
  input  Cin,
  input  A_0,
  input  B_0,
  input  A_1,
  input  B_1,
  input  A_2,
  input  B_2,
  input  A_3,
  input  B_3,
  input  A_0_2,
  input  B_0_2,
  input  A_0_3,
  input  B_0_3,
  input  A_0_4,
  input  B_0_4,
  input  A_0_5,
  input  B_0_5,
  output Q_O,
  output Q_O_2,
  output Q_O_3,
  output Q_O_4,
  output Q_O_5,
  output Q_O_6,
  output Q_O_7,
  output Q_O_8,
  output Cout
);

  wire main_1_cout, main_2_cout, main_2_q0, main_2_q1, main_2_q2, main_2_q3, main_3_cout, main_3_q0,
       main_3_q1, main_3_q2, main_3_q3;

  SOMADOR_RCA_4_Bits_main main_1 (
    .Cin(Cin), .A0(A_0), .B0(B_0), .A1(A_1), .B1(B_1), .A2(A_2), .B2(B_2), .A3(A_3), .B3(B_3), .Q0(Q_O),
    .Q1(Q_O_2), .Q2(Q_O_3), .Q3(Q_O_4), .Cout(main_1_cout));
  SOMADOR_RCA_4_Bits_main main_2 (
    .Cin(1'b0), .A0(A_0_2), .B0(B_0_2), .A1(A_0_3), .B1(B_0_3), .A2(A_0_4), .B2(B_0_4), .A3(A_0_5),
    .B3(B_0_5), .Q0(main_2_q0), .Q1(main_2_q1), .Q2(main_2_q2), .Q3(main_2_q3), .Cout(main_2_cout));
  SOMADOR_RCA_4_Bits_main main_3 (
    .Cin(1'b1), .A0(A_0_2), .B0(B_0_2), .A1(A_0_3), .B1(B_0_3), .A2(A_0_4), .B2(B_0_4), .A3(A_0_5),
    .B3(B_0_5), .Q0(main_3_q0), .Q1(main_3_q1), .Q2(main_3_q2), .Q3(main_3_q3), .Cout(main_3_cout));
  // MUX_2_X_1_5_BITS_main main_4: pin names not known; wires that end beside it: main_2_q0, main_2_q1, main_2_q2, main_2_q3, main_2_cout, main_3_q0, main_3_q1, main_3_q2, main_3_q3, main_3_cout, main_1_cout, Q_O_5, Q_O_6, Q_O_7, Q_O_8, Cout
endmodule
