// Logisim project SOMADOR RCA 4 Bits.circ as structural Verilog: 1 circuit, main circuit main
// RCA
module main (
  input  Cin,
  input  A0,
  input  B0,
  input  A1,
  input  B1,
  input  A2,
  input  B2,
  input  A3,
  input  B3,
  output Q0,
  output Q1,
  output Q2,
  output Q3,
  output Cout
);

  wire _1_out, _3_out, _4_out, _5_out, _6_out, _8_out, _9_out, _10_out, _11_out, _13_out, _14_out, _15_out,
       _16_out, _18_out, _19_out;

  xor _1 (_1_out, B0, A0);
  and _4 (_4_out, A0, B0);
  xor _6 (_6_out, B1, A1);
  and _9 (_9_out, A1, B1);
  xor _11 (_11_out, B2, A2);
  and _14 (_14_out, A2, B2);
  xor _16 (_16_out, B3, A3);
  and _19 (_19_out, A3, B3);
  and _3 (_3_out, Cin, _1_out);
  and _8 (_8_out, _5_out, _6_out);
  and _13 (_13_out, _10_out, _11_out);
  and _18 (_18_out, _15_out, _16_out);
  xor _2 (Q0, Cin, _1_out);
  or _5 (_5_out, _3_out, _4_out);
  xor _7 (Q1, _5_out, _6_out);
  or _10 (_10_out, _8_out, _9_out);
  xor _12 (Q2, _10_out, _11_out);
  or _15 (_15_out, _13_out, _14_out);
  xor _17 (Q3, _15_out, _16_out);
  or _20 (Cout, _18_out, _19_out);
endmodule
